// Logisim project shifter8x4JZukoff.circ as structural Verilog: 2 circuits, main circuit main
module main (
  input  [7:0] in_1,
  input  [1:0] in_2,
  output [7:0] out_3
);

  shifter8x4 shifter8x4_1 (.in_1(in_1), .in_2(in_2), .out_3(out_3));
endmodule

module shifter8x4 (
  input  [7:0] in_1,
  input  [1:0] in_2,
  output [7:0] out_3
);

  wire [7:6] undriven;
  wire [7:7] undriven_2;

  Multiplexer #(.select(2), .width(8)) multiplexer_1 (
    .in0({in_1[6:4], {4{in_1[7]}}, 1'b0}), .in1({undriven, in_1[7:4], {2{in_1[7]}}}),
    .in2({undriven_2[7], in_1[7:4], {3{in_1[7]}}}), .in3({in_1[7:4], {4{in_1[7]}}}), .out(out_3), .sel(in_2));

  assign in_1[3:0] = {4{in_1[7]}};
  // also tied to GND on the sheet: in_1[7]
endmodule
