// Logisim project garage.circ as structural Verilog: 2 circuits, main circuit NextState_0
module NextState_0 (
  input  CurrentState_1,
  input  CurrentState_0,
  input  Top,
  input  Bottom,
  input  Eye,
  input  Go,
  output NextState_1,
  output NextState_0
);

  wire and_1_out, and_2_out, and_3_out, and_4_out, and_5_out, and_6_out, and_7_out, and_8_out, and_9_out,
       and_10_out, and_11_out, and_12_out, not_1_out, not_2_out, not_3_out, not_4_out, not_5_out, not_6_out,
       not_7_out, not_8_out, not_9_out, not_10_out, not_11_out, not_12_out, not_13_out, not_14_out,
       not_15_out;

  not not_1 (not_1_out, CurrentState_1);
  not not_2 (not_2_out, Bottom);
  not not_3 (not_3_out, Bottom);
  not not_4 (not_4_out, CurrentState_0);
  not not_5 (not_5_out, Bottom);
  not not_6 (not_6_out, Go);
  not not_7 (not_7_out, Eye);
  not not_8 (not_8_out, CurrentState_1);
  not not_9 (not_9_out, Top);
  not not_10 (not_10_out, CurrentState_1);
  not not_11 (not_11_out, Top);
  not not_12 (not_12_out, Go);
  not not_13 (not_13_out, Eye);
  not not_14 (not_14_out, Bottom);
  not not_15 (not_15_out, Bottom);
  and and_1 (and_1_out, not_1_out, CurrentState_0, not_2_out, Go);
  and and_2 (and_2_out, CurrentState_0, Top, not_3_out);
  and and_3 (and_3_out, CurrentState_1, not_4_out);
  and and_4 (and_4_out, CurrentState_1, not_5_out, Eye, not_6_out);
  and and_5 (and_5_out, CurrentState_1, Bottom, not_7_out);
  and and_6 (and_6_out, CurrentState_1, Top);
  and and_7 (and_7_out, not_8_out, not_9_out, Bottom, Go);
  and and_8 (and_8_out, not_10_out, CurrentState_0, not_11_out, not_12_out);
  and and_9 (and_9_out, CurrentState_0, Bottom, not_13_out);
  and and_10 (and_10_out, CurrentState_0, Top, Bottom);
  and and_11 (and_11_out, CurrentState_1, not_14_out, Eye, Go);
  and and_12 (and_12_out, CurrentState_1, CurrentState_0, not_15_out);
  or or_1 (NextState_1, and_1_out, and_2_out, and_3_out, and_4_out, and_5_out, and_6_out);
  or or_2 (NextState_0, and_7_out, and_8_out, and_9_out, and_10_out, and_11_out, and_12_out);
endmodule

module Output_0 (
  input  CurrentState_1,
  input  CurrentState_0,
  output Up,
  output Down
);

  wire not_1_out;

  not not_1 (not_1_out, CurrentState_1);
  and and_1 (Down, CurrentState_1, CurrentState_0);
  and and_2 (Up, not_1_out, CurrentState_0);
endmodule
