// Logisim project main.circ as structural Verilog: 4 circuits, main circuit main
module main (
  input  Top,
  input  Bottom,
  input  Eye,
  input  Go,
  input  Reset,
  output Up,
  output Down
);

  wire Clock_out;
  wire [1:0] nextstate_1_nextstate, register_1_q;
  wire [3:3] oneshot_1_out_3;

  Clock Clock (.out(Clock_out));
  OneShot oneshot_1 (.in_1(Go), .Clock(Clock_out), .out_3(oneshot_1_out_3[3]));
  NextState nextstate_1 (
    .Inputs({oneshot_1_out_3[3], Eye, Bottom, Top}), .CurrentState(register_1_q),
    .NextState(nextstate_1_nextstate));
  Output output_1 (.CurrentState(register_1_q), .Output({Down, Up}));
  Register #(.width(2)) register_1 (
    .D(nextstate_1_nextstate), .Q(register_1_q), .clk(Clock_out), .clr(Reset));  // open: en

  // Notes on the sheet:
  //   OneShot
  //   NextState
  //   Output
endmodule

module OneShot (
  input  in_1,
  input  Clock,
  output out_3
);

  wire and_2_out, and_3_out, and_4_out, d_ff_1_q, d_ff_2_q, not_1_out, not_2_out, not_3_out, not_4_out,
       not_5_out, or_1_out;

  D_Flip_Flop d_ff_1 (.clk(Clock), .D(and_2_out), .Q(d_ff_1_q));  // open: Qn, preset, en, reset
  D_Flip_Flop d_ff_2 (.clk(Clock), .D(or_1_out), .Q(d_ff_2_q));  // open: Qn, preset, en, reset
  and and_1 (out_3, d_ff_1_q, not_1_out);
  not not_1 (not_1_out, d_ff_2_q);
  not not_2 (not_2_out, d_ff_1_q);
  and and_2 (and_2_out, in_1, not_2_out, not_3_out);
  not not_3 (not_3_out, d_ff_2_q);
  and and_3 (and_3_out, in_1, d_ff_1_q, not_4_out);
  not not_4 (not_4_out, d_ff_2_q);
  and and_4 (and_4_out, in_1, not_5_out, d_ff_2_q);
  not not_5 (not_5_out, d_ff_1_q);
  or or_1 (or_1_out, and_3_out, and_4_out);

  // Notes on the sheet:
  //   state register
  //   output
  //   next state
  //   When the input of this circuit is true,
  //   the output will be true.
  //   The output will return to false after
  //   one clock cycle, even if the input remains
  //   true longer than one clock cycle.
endmodule

module NextState (
  input  [3:0] Inputs,
  input  [1:0] CurrentState,
  output [1:0] NextState
);

  NextState_0 nextstate_0_1 (
    .CurrentState_1(CurrentState[1]), .CurrentState_0(CurrentState[0]), .Top(Inputs[0]), .Bottom(Inputs[1]),
    .Eye(Inputs[2]), .Go(Inputs[3]), .NextState_1(NextState[1]), .NextState_0(NextState[0]));
endmodule

module Output (
  input  [1:0] CurrentState,
  output [1:0] Output
);

  Output_0 output_0_1 (
    .CurrentState_1(CurrentState[1]), .CurrentState_0(CurrentState[0]), .Up(Output[0]), .Down(Output[1]));
endmodule
