// Logisim project datapathJZukoff.circ as structural Verilog: 1 circuit, main circuit Datapath
module Datapath (
  input  Reset,
  input  Clear,
  input  Clear_2
);

  wire alu_1_zero, and_1_out, and_2_out, and_3_out, Clock_out, control_1_p2, control_1_p3, control_1_p4,
       control_1_p5, control_1_p6, control_1_p7, control_1_p8, control_1_p9, control_1_p10, not_1_out;
  wire [3:0] alucontrol_1_p4;
  wire [4:0] instructiondecode_1_rd, instructiondecode_1_rs, instructiondecode_1_rt, multiplexer_1_out;
  wire [5:0] control_1_p1, instructiondecode_1_funct;
  wire [7:0] wordaddress_1_wordaddress, wordaddress_2_wordaddress;
  wire [15:0] instructiondecode_1_immediate;
  wire [25:0] instructiondecode_1_address;
  wire [31:0] adder_1_out, alu_1_result, branchaddress_1_branchaddress, jumpaddress_1_jumpaddress,
       memorydata_1_readdata, memorydata_1_tomemory, multiplexer_2_out, multiplexer_3_out, multiplexer_4_out,
       multiplexer_5_out, ram_1_data, register_1_q, registers_1_readdata1, registers_1_readdata2,
       signextend_1_out_2;

  WordAddress wordaddress_1 (.ByteAddress(register_1_q), .WordAddress(wordaddress_1_wordaddress));  // open: Unaligned
  Clock Clock (.out(Clock_out));
  Register #(.width(32)) register_1 (
    .D(multiplexer_5_out), .Q(register_1_q), .clk(Clock_out), .clr(Reset));  // open: en
  RAM #(.dataWidth(32)) ram_1 (
    .addr(wordaddress_1_wordaddress), .data(ram_1_data), .sel(1'b1), .clk(1'b0), .ld(1'b1), .clr(Clear));
  // Control control_1: pin names not known; wires that end beside it: control_1_p1, control_1_p2, control_1_p3, control_1_p4, control_1_p5, control_1_p6, control_1_p7, control_1_p8, control_1_p9, control_1_p10
  InstructionDecode instructiondecode_1 (
    .Instruction(ram_1_data), .op(control_1_p1), .rs(instructiondecode_1_rs), .rt(instructiondecode_1_rt),
    .rd(instructiondecode_1_rd), .funct(instructiondecode_1_funct),
    .immediate(instructiondecode_1_immediate), .address(instructiondecode_1_address));  // open: shamt
  Multiplexer #(.width(5)) multiplexer_1 (
    .in0(instructiondecode_1_rt), .in1(instructiondecode_1_rd), .out(multiplexer_1_out), .sel(control_1_p2));
  not not_1 (not_1_out, Clock_out);
  Adder #(.width(32)) adder_1 (.a(32'h4), .b(register_1_q), .out(adder_1_out));  // open: cin, cout
  Registers registers_1 (
    .ReadRegister1(instructiondecode_1_rs), .ReadRegister2(instructiondecode_1_rt),
    .WriteRegister(multiplexer_1_out), .WriteData(multiplexer_3_out), .Write(and_1_out), .Clear(Reset),
    .ReadData1(registers_1_readdata1), .ReadData2(registers_1_readdata2));
  SignExtend signextend_1 (.in_1(instructiondecode_1_immediate), .out_2(signextend_1_out_2));
  and and_1 (and_1_out, control_1_p10, not_1_out);
  WordAddress wordaddress_2 (.ByteAddress(alu_1_result), .WordAddress(wordaddress_2_wordaddress));  // open: Unaligned
  BranchAddress branchaddress_1 (
    .PC_4(adder_1_out), .Address(signextend_1_out_2), .BranchAddress(branchaddress_1_branchaddress));
  Multiplexer #(.width(32)) multiplexer_2 (
    .in0(registers_1_readdata2), .in1(signextend_1_out_2), .out(multiplexer_2_out), .sel(control_1_p9));
  ALU alu_1 (
    .A(registers_1_readdata1), .B(multiplexer_2_out), .Operation(alucontrol_1_p4), .Zero(alu_1_zero),
    .Result(alu_1_result));  // open: Overflow
  // ALUcontrol alucontrol_1: pin names not known; wires that end beside it: registers_1_readdata2, instructiondecode_1_funct, control_1_p7, alucontrol_1_p4
  and and_2 (and_2_out, not_1_out, control_1_p8);
  and and_3 (and_3_out, control_1_p3, alu_1_zero);
  Multiplexer #(.width(32)) multiplexer_3 (
    .in0(alu_1_result), .in1(memorydata_1_readdata), .out(multiplexer_3_out), .sel(control_1_p6));
  MemoryData memorydata_1 (
    .WriteData(registers_1_readdata2), .FromMemory(memorydata_1_tomemory), .Write(control_1_p8),
    .Read(control_1_p5), .ReadData(memorydata_1_readdata), .ToMemory(memorydata_1_tomemory));
  RAM #(.dataWidth(32)) ram_2 (
    .addr(wordaddress_2_wordaddress), .data(memorydata_1_tomemory), .sel(1'b1), .clk(and_2_out),
    .ld(control_1_p5), .clr(Clear_2));
  Multiplexer #(.width(32)) multiplexer_4 (
    .in0(adder_1_out), .in1(branchaddress_1_branchaddress), .out(multiplexer_4_out), .sel(and_3_out));
  JumpAddress jumpaddress_1 (
    .Address(instructiondecode_1_address), .PC_4(adder_1_out), .JumpAddress(jumpaddress_1_jumpaddress));
  Multiplexer #(.width(32)) multiplexer_5 (
    .in0(multiplexer_4_out), .in1(jumpaddress_1_jumpaddress), .out(multiplexer_5_out), .sel(control_1_p4));

  // Notes on the sheet:
  //   Josh Zukoff
  //   10/25/10
  //   Instruction Memory
  //   Decode
  //   PC
  //   Control
  //   Registers
  //   Extend
  //   Branch
  //   ALU
  //   ALU control
  //   Data Memory
endmodule
