// Logisim project datapath.circ as structural Verilog: 1 circuit, main circuit Datapath
module Datapath (
  input  Reset,
  input  Clear,
  input  Clear_2
);

  wire and_1_out, and_2_out, Clock_out, fake_control_1_p1, fake_control_1_p2, fake_control_1_p3,
       fake_control_1_p4, not_1_out;
  wire [7:0] wordaddress_1_wordaddress, wordaddress_2_wordaddress;
  wire [31:0] alu_1_result, fake_alucontrol_1_p2, memorydata_1_tomemory, ram_1_data, register_1_q,
       registers_1_readdata2;

  WordAddress wordaddress_1 (.ByteAddress(register_1_q), .WordAddress(wordaddress_1_wordaddress));  // open: Unaligned
  Clock #(.highDuration(1), .lowDuration(1)) Clock (.out(Clock_out));
  Register #(.width(32), .trigger("rising")) register_1 (
    .Q(register_1_q), .clk(Clock_out), .clr(Reset));  // open: D, en
  RAM #(.addrWidth(8), .dataWidth(32), .bus("combined")) ram_1 (
    .addr(wordaddress_1_wordaddress), .data(ram_1_data), .sel(1'b1), .clk(1'b0), .ld(1'b1), .clr(Clear));
  // Fake_Control fake_control_1: pin names not known; wires that end beside it: fake_control_1_p1, fake_control_1_p2, fake_control_1_p3, fake_control_1_p4
  InstructionDecode instructiondecode_1 (.Instruction(ram_1_data));  // open: op, rs, rt, rd, shamt, funct, immediate, address
  not not_1 (not_1_out, Clock_out);
  Adder #(.width(32)) adder_1 (.a(32'h4));  // open: b, out, cin, cout
  Registers registers_1 (
    .Write(and_1_out), .Clear(Reset), .ReadData2(registers_1_readdata2));  // open: ReadRegister1, ReadRegister2, WriteRegister, WriteData, ReadData1
  // SignExtend signextend_1: pin names not known
  and and_1 (and_1_out, fake_control_1_p4, not_1_out);
  WordAddress wordaddress_2 (.ByteAddress(alu_1_result), .WordAddress(wordaddress_2_wordaddress));  // open: Unaligned
  // BranchAddress branchaddress_1: pin names not known
  ALU alu_1 (.Result(alu_1_result));  // open: A, B, Operation, Zero, Overflow
  // Fake_ALUcontrol fake_alucontrol_1: pin names not known; wires that end beside it: fake_control_1_p2, fake_alucontrol_1_p2
  and and_2 (and_2_out, not_1_out, fake_control_1_p3);
  MemoryData memorydata_1 (
    .WriteData(registers_1_readdata2), .FromMemory(memorydata_1_tomemory), .Write(fake_control_1_p3),
    .Read(fake_control_1_p1), .ReadData(fake_alucontrol_1_p2), .ToMemory(memorydata_1_tomemory));
  RAM #(.addrWidth(8), .dataWidth(32), .bus("combined")) ram_2 (
    .addr(wordaddress_2_wordaddress), .data(memorydata_1_tomemory), .sel(1'b1), .clk(and_2_out),
    .ld(fake_control_1_p1), .clr(Clear_2));

  // Notes on the sheet:
  //   Your Name
  //   Today's Date
  //   Instruction Memory
  //   Decode
  //   PC
  //   Control
  //   Registers
  //   Extend
  //   Branch
  //   ALU
  //   ALU control
  //   Data Memory
endmodule
