// Logisim project pipeline1JZukoff.circ as structural Verilog: 1 circuit, main circuit Datapath
module Datapath (
  input  Reset,
  input  Clear,
  input  Clear_2
);

  wire alu_1_zero, and_1_out, and_2_out, and_3_out, Clock_out, not_1_out, or_1_out, Zero_q;
  wire [1:0] control_1_aluop, WB_2_q, WB_q;
  wire [3:0] alucontrol_1_operation, control_1_regdst, EX_q, M_q;
  wire [4:0] control_1_regwrite, instructiondecode_1_rd, instructiondecode_1_rs, instructiondecode_1_rt,
       multiplexer_3_out, RD_q, RT_q, RT_RD_2_q, RT_RD_q, WB_M_q;
  wire [5:0] Funct_q, instructiondecode_1_funct, instructiondecode_1_op;
  wire [7:0] wordaddress_1_wordaddress, wordaddress_2_wordaddress;
  wire [15:0] instructiondecode_1_immediate;
  wire [25:0] instructiondecode_1_address, Jump_Address_q;
  wire [31:0] adder_1_out, alu_1_result, ALU_Result_2_q, ALU_Result_q, Branch_q,
       branchaddress_1_branchaddress, Extend_q, Instruction_q, Jump_q, jumpaddress_1_jumpaddress,
       memorydata_1_readdata, memorydata_1_tomemory, multiplexer_1_out, multiplexer_2_out, multiplexer_4_out,
       multiplexer_5_out, multiplexer_6_out, PC_4_2_q, PC_4_3_q, PC_4_q, ram_1_data, Read1_q, Read2_2_q,
       Read2_q, Read_Data_q, register_1_q, registers_1_readdata1, registers_1_readdata2, signextend_1_out_2;

  Multiplexer #(.width(32)) multiplexer_1 (
    .in0(adder_1_out), .in1(multiplexer_5_out), .out(multiplexer_1_out), .sel(or_1_out));
  WordAddress wordaddress_1 (.ByteAddress(register_1_q), .WordAddress(wordaddress_1_wordaddress));  // open: Unaligned
  Register #(.width(32)) register_1 (
    .D(multiplexer_1_out), .Q(register_1_q), .clk(Clock_out), .clr(Reset));  // open: en
  Clock Clock (.out(Clock_out));
  Adder #(.width(32)) adder_1 (.a(32'h4), .b(register_1_q), .out(adder_1_out));  // open: cin, cout
  RAM #(.dataWidth(32)) ram_1 (
    .addr(wordaddress_1_wordaddress), .data(ram_1_data), .sel(1'b1), .clk(1'b0), .ld(1'b1), .clr(Clear));
  Register #(.width(32)) PC_4 (.D(adder_1_out), .Q(PC_4_q), .clk(Clock_out), .clr(Reset));  // open: en
  Register #(.width(32)) Instruction (.D(ram_1_data), .Q(Instruction_q), .clk(Clock_out), .clr(Reset));  // open: en
  Control control_1 (
    .op(instructiondecode_1_op), .RegDst(control_1_regdst[0]), .Branch(control_1_regwrite[1]),
    .Jump(control_1_regwrite[4]), .MemRead(control_1_regwrite[2]), .ALUop(control_1_aluop),
    .MemWrite(control_1_regwrite[3]), .ALUsrc(control_1_regdst[3]), .RegWrite(control_1_regwrite[0]));  // open: MemToReg
  InstructionDecode instructiondecode_1 (
    .Instruction(Instruction_q), .op(instructiondecode_1_op), .rs(instructiondecode_1_rs),
    .rt(instructiondecode_1_rt), .rd(instructiondecode_1_rd), .funct(instructiondecode_1_funct),
    .immediate(instructiondecode_1_immediate), .address(instructiondecode_1_address));  // open: shamt
  not not_1 (not_1_out, Clock_out);
  Registers registers_1 (
    .ReadRegister1(instructiondecode_1_rs), .ReadRegister2(instructiondecode_1_rt),
    .WriteRegister(RT_RD_2_q), .WriteData(multiplexer_6_out), .Write(and_1_out), .Clear(Reset),
    .ReadData1(registers_1_readdata1), .ReadData2(registers_1_readdata2));
  SignExtend signextend_1 (.in_1(instructiondecode_1_immediate), .out_2(signextend_1_out_2));
  and and_1 (and_1_out, WB_2_q[0], not_1_out);
  Register #(.width(5)) WB_M (.D(control_1_regwrite), .Q(WB_M_q), .clk(Clock_out), .clr(Reset));  // open: en
  Register #(.width(4)) EX (
    .D({control_1_regdst[3], control_1_aluop, control_1_regdst[0]}), .Q(EX_q), .clk(Clock_out), .clr(Reset));  // open: en
  Register #(.width(32)) PC_4_2 (.D(PC_4_q), .Q(PC_4_2_q), .clk(Clock_out), .clr(Reset));  // open: en
  Register #(.width(32)) Read1 (.D(registers_1_readdata1), .Q(Read1_q), .clk(Clock_out), .clr(Reset));  // open: en
  Register #(.width(32)) Read2 (.D(registers_1_readdata2), .Q(Read2_q), .clk(Clock_out), .clr(Reset));  // open: en
  Register #(.width(32)) Extend (.D(signextend_1_out_2), .Q(Extend_q), .clk(Clock_out), .clr(Reset));  // open: en
  Register #(.width(6)) Funct (.D(instructiondecode_1_funct), .Q(Funct_q), .clk(Clock_out), .clr(Reset));  // open: en
  Register #(.width(5)) RT (.D(instructiondecode_1_rt), .Q(RT_q), .clk(Clock_out), .clr(Reset));  // open: en
  Register #(.width(5)) RD (.D(instructiondecode_1_rd), .Q(RD_q), .clk(Clock_out), .clr(Reset));  // open: en
  Register #(.width(26)) Jump_Address (
    .D(instructiondecode_1_address), .Q(Jump_Address_q), .clk(Clock_out), .clr(Reset));  // open: en
  Multiplexer #(.width(32)) multiplexer_2 (.in0(Read2_q), .in1(Extend_q), .out(multiplexer_2_out), .sel(EX_q[3]));
  ALUcontrol alucontrol_1 (.funct(Funct_q), .ALUop(EX_q[2:1]), .Operation(alucontrol_1_operation));
  Multiplexer #(.width(5)) multiplexer_3 (.in0(RT_q), .in1(RD_q), .out(multiplexer_3_out), .sel(EX_q[0]));
  BranchAddress branchaddress_1 (.PC_4(PC_4_2_q), .Address(Extend_q), .BranchAddress(branchaddress_1_branchaddress));
  JumpAddress jumpaddress_1 (.Address(Jump_Address_q), .PC_4(PC_4_2_q), .JumpAddress(jumpaddress_1_jumpaddress));
  ALU alu_1 (
    .A(Read1_q), .B(multiplexer_2_out), .Operation(alucontrol_1_operation), .Zero(alu_1_zero),
    .Result(alu_1_result));  // open: Overflow
  Register #(.width(1)) WB (.D(WB_M_q[0]), .Q(WB_q[0]), .clk(Clock_out));  // open: en, clr
  Register #(.width(4)) M (.D(WB_M_q[4:1]), .Q({M_q[3:2], WB_q[1], M_q[0]}), .clk(Clock_out), .clr(Reset));  // open: en
  Register #(.width(32)) PC_4_3 (.D(PC_4_2_q), .Q(PC_4_3_q), .clk(Clock_out), .clr(Reset));  // open: en
  Register #(.width(32)) Branch (
    .D(branchaddress_1_branchaddress), .Q(Branch_q), .clk(Clock_out), .clr(Reset));  // open: en
  Register #(.width(32)) Jump (.D(jumpaddress_1_jumpaddress), .Q(Jump_q), .clk(Clock_out), .clr(Reset));  // open: en
  Register #(.width(1)) Zero (.D(alu_1_zero), .Q(Zero_q), .clk(Clock_out), .clr(Reset));  // open: en
  Register #(.width(32)) ALU_Result (.D(alu_1_result), .Q(ALU_Result_q), .clk(Clock_out), .clr(Reset));  // open: en
  Register #(.width(32)) Read2_2 (.D(Read2_q), .Q(Read2_2_q), .clk(Clock_out), .clr(Reset));  // open: en
  Register #(.width(5)) RT_RD (.D(multiplexer_3_out), .Q(RT_RD_q), .clk(Clock_out), .clr(Reset));  // open: en
  Multiplexer #(.width(32)) multiplexer_4 (.in0(PC_4_3_q), .in1(Branch_q), .out(multiplexer_4_out), .sel(and_2_out));
  and and_2 (and_2_out, Zero_q, M_q[0]);
  WordAddress wordaddress_2 (.ByteAddress(ALU_Result_q), .WordAddress(wordaddress_2_wordaddress));  // open: Unaligned
  or or_1 (or_1_out, M_q[0], M_q[3]);
  Multiplexer #(.width(32)) multiplexer_5 (
    .in0(multiplexer_4_out), .in1(Jump_q), .out(multiplexer_5_out), .sel(M_q[3]));
  and and_3 (and_3_out, not_1_out, M_q[2]);
  MemoryData memorydata_1 (
    .WriteData(Read2_2_q), .FromMemory(memorydata_1_tomemory), .Write(M_q[2]), .Read(WB_q[1]),
    .ReadData(memorydata_1_readdata), .ToMemory(memorydata_1_tomemory));
  RAM #(.dataWidth(32)) ram_2 (
    .addr(wordaddress_2_wordaddress), .data(memorydata_1_tomemory), .sel(1'b1), .clk(and_3_out),
    .ld(WB_q[1]), .clr(Clear_2));
  Register #(.width(2)) WB_2 (.D(WB_q), .Q(WB_2_q), .clk(Clock_out), .clr(Reset));  // open: en
  Register #(.width(32)) ALU_Result_2 (.D(ALU_Result_q), .Q(ALU_Result_2_q), .clk(Clock_out), .clr(Reset));  // open: en
  Register #(.width(32)) Read_Data (
    .D(memorydata_1_readdata), .Q(Read_Data_q), .clk(Clock_out), .clr(Reset));  // open: en
  Register #(.width(5)) RT_RD_2 (.D(RT_RD_q), .Q(RT_RD_2_q), .clk(Clock_out), .clr(Reset));  // open: en
  Multiplexer #(.width(32)) multiplexer_6 (
    .in0(ALU_Result_2_q), .in1(Read_Data_q), .out(multiplexer_6_out), .sel(WB_2_q[1]));

  // Notes on the sheet:
  //   Josh Zukoff
  //   November 6
  //   PC
  //   Instruction Memory
  //   Decode
  //   Control
  //   Extend
  //   ALU
  //   Data Memory
endmodule
