// Logisim project controlJZukoff.circ as structural Verilog: 7 circuits, main circuit ALUcontrol_0
module ALUcontrol_0 (
  input  ALUop_1,
  input  ALUop_0,
  input  F5,
  input  F4,
  input  F3,
  input  F2,
  input  F1,
  input  F0,
  output Operation_3,
  output Operation_2,
  output Operation_1,
  output Operation_0
);

  wire and_1_out, and_2_out, and_3_out, and_4_out, and_5_out, and_6_out, and_7_out, not_1_out, not_2_out,
       not_3_out, not_4_out, not_5_out;

  not not_1 (not_1_out, ALUop_1);
  not not_2 (not_2_out, ALUop_0);
  not not_3 (not_3_out, F3);
  not not_4 (not_4_out, F2);
  not not_5 (not_5_out, F1);
  and and_1 (and_1_out, ALUop_1, ALUop_0);
  and and_2 (and_2_out, not_1_out, not_2_out);
  and and_3 (and_3_out, not_1_out, ALUop_0);
  and and_4 (and_4_out, F3, not_2_out, ALUop_1);
  and and_5 (and_5_out, not_3_out, not_4_out, not_5_out, not_2_out, ALUop_1);
  and and_6 (and_6_out, F1, not_2_out, ALUop_1);
  and and_7 (and_7_out, not_2_out, ALUop_1, F0);
  or or_1 (Operation_2, and_4_out, and_6_out, and_3_out);
  or or_2 (Operation_1, and_2_out, and_5_out, and_4_out, and_3_out, and_6_out);
  or or_3 (Operation_0, and_1_out, and_4_out, and_7_out);

  assign Operation_3 = 1'b0;
endmodule

module Control_0 (
  input  op_5,
  input  op_4,
  input  op_3,
  input  op_2,
  input  op_1,
  input  op_0,
  output RegDst,
  output Branch,
  output Jump,
  output MemRead,
  output MemToReg,
  output MemWrite,
  output ALUsrc,
  output RegWrite
);

  wire and_6_out, not_1_out, not_2_out, not_3_out, not_4_out, not_5_out, not_6_out;

  not not_1 (not_1_out, op_5);
  not not_2 (not_2_out, op_4);
  not not_3 (not_3_out, op_3);
  not not_4 (not_4_out, op_2);
  not not_5 (not_5_out, op_1);
  not not_6 (not_6_out, op_0);
  and and_1 (Branch, not_6_out, not_5_out, op_2, not_3_out, not_1_out, not_2_out);
  and and_2 (MemRead, op_5, not_3_out);
  and and_3 (MemWrite, op_5, op_3);
  and and_4 (RegDst, not_1_out, not_2_out, not_3_out, not_4_out, not_5_out, not_6_out);
  and and_5 (Jump, op_1, not_3_out, not_6_out, not_2_out, not_1_out, not_4_out);
  and and_6 (and_6_out, not_1_out, op_3);
  or or_1 (ALUsrc, MemWrite, MemRead, and_6_out);
  or or_2 (RegWrite, MemRead, RegDst, and_6_out);

  assign MemToReg = MemRead;
endmodule

module Control_1 (
  input  op_5,
  input  op_4,
  input  op_3,
  input  op_2,
  input  op_1,
  input  op_0,
  output ALUop_1,
  output ALUop_0
);

  wire and_1_out, and_2_out, and_3_out, not_1_out, not_2_out, not_3_out, not_4_out, not_5_out, not_6_out;

  not not_1 (not_1_out, op_5);
  not not_2 (not_2_out, op_4);
  not not_3 (not_3_out, op_3);
  not not_4 (not_4_out, op_2);
  not not_5 (not_5_out, op_1);
  not not_6 (not_6_out, op_0);
  and and_1 (and_1_out, op_2, op_0, not_1_out);
  and and_2 (and_2_out, not_1_out, op_2, not_6_out);
  and and_3 (and_3_out, not_1_out, not_2_out, not_3_out, not_4_out, not_5_out, not_6_out);
  or or_1 (ALUop_1, and_3_out, and_1_out);
  or or_2 (ALUop_0, and_1_out, and_2_out);
endmodule

module Fake_Control (
  input  [9:0] test,
  input  [5:0] op,
  output RegDst,
  output Branch,
  output Jump,
  output MemRead,
  output MemToReg,
  output [1:0] ALUop,
  output MemWrite,
  output ALUsrc,
  output RegWrite
);


  assign ALUop = {test[3], test[4]};
  assign ALUsrc = test[1];
  assign Branch = test[8];
  assign Jump = test[7];
  assign MemRead = test[6];
  assign MemToReg = test[5];
  assign MemWrite = test[2];
  assign RegDst = test[9];
  assign RegWrite = test[0];
endmodule

module Fake_ALUcontrol (
  input  [3:0] test,
  input  [5:0] funct,
  input  [1:0] ALUop,
  output [3:0] Operation
);


  assign Operation = test;
endmodule

module Control (
  input  [5:0] op,
  output RegDst,
  output Branch,
  output Jump,
  output MemRead,
  output MemToReg,
  output [1:0] ALUop,
  output MemWrite,
  output ALUsrc,
  output RegWrite
);

  Control_0 control_0_1 (
    .op_5(op[5]), .op_4(op[4]), .op_3(op[3]), .op_2(op[2]), .op_1(op[1]), .op_0(op[0]), .RegDst(RegDst),
    .Branch(Branch), .Jump(Jump), .MemRead(MemRead), .MemToReg(MemToReg), .MemWrite(MemWrite),
    .ALUsrc(ALUsrc), .RegWrite(RegWrite));
  Control_1 control_1_1 (
    .op_5(op[5]), .op_4(op[4]), .op_3(op[3]), .op_2(op[2]), .op_1(op[1]), .op_0(op[0]), .ALUop_1(ALUop[1]),
    .ALUop_0(ALUop[0]));
endmodule

module ALUcontrol (
  input  [5:0] funct,
  input  [1:0] ALUop,
  output [3:0] Operation
);

  ALUcontrol_0 alucontrol_0_1 (
    .ALUop_1(ALUop[1]), .ALUop_0(ALUop[0]), .F5(funct[5]), .F4(funct[4]), .F3(funct[3]), .F2(funct[2]),
    .F1(funct[1]), .F0(funct[0]), .Operation_3(Operation[3]), .Operation_2(Operation[2]),
    .Operation_1(Operation[1]), .Operation_0(Operation[0]));
endmodule
